# Fritzing sketch trafficLights (saved by Fritzing 0.9.1b)
breadboards: 1

parts:
  Part1 = Arduino Uno (Rev3)
  LED1 = LED - 5mm [color="Red (633nm)" package="5 mm [THT]"]
  LED2 = LED - 5mm [color="Orange (612nm)" package="5 mm [THT]"]
  LED3 = LED - 5mm [color="Green (565nm)" package="5 mm [THT]"]

nets:
  N1: Part1.D9_PWM, LED3.anode
  N2: Part1.D10_PWM/SS, LED2.anode
  N3: Part1.D11_PWM/MOSI, LED1.anode
  N4: Part1.GND, LED1.cathode, LED2.cathode, LED3.cathode

// code stored in the sketch: trafficLights.ino
int RED = 11;
int ORANGE = 10;
int GREEN = 9;

void setup(){
  pinMode(RED, OUTPUT);
  pinMode(ORANGE, OUTPUT);
  pinMode(GREEN, OUTPUT);
}

void loop(){
  digitalWrite(RED, HIGH);
}
